# Fritzing sketch LPOS-enhed (saved by Fritzing 0.9.6b)
breadboards: 1

parts:
  Mod1 = Arduino MKR Wifi 1010
  M1 = Heart Rate Sensor
  S2 = Pushbutton [package="[THT]"]
  J1 = Piezo Speaker
  R1 = Resistor [tolerance=±5% resistance=220 package="0603 [SMD]"]
  LED1 = LED - 5mm [color="Red (633nm)" current=0.030 package="5 mm [THT]"]
  R2 = Resistor [tolerance=±5% resistance=220 package="0603 [SMD]"]

nets:
  GND: Mod1.GND, M1.GND, S2.Pin_3, S2.Pin_4, J1.pin1, LED1.cathode
  N1: Mod1.A1, M1.SIG
  N2: Mod1.D1, R1.Pin_0
  N3: Mod1.D6, R2.Pin_0
  N4: Mod1.D7, S2.Pin_1, S2.Pin_2
  +5V: Mod1.+5V, M1.VCC
  N5: J1.pin2, R1.Pin_1
  N6: LED1.anode, R2.Pin_1

notes:
  Changed to "A" for analog.

custom parts:
  Arduino MKR Wifi 1010: Arduino MKR Wifi 1010, SAMD21 Cortex-M0+ 32bit Low Power ARM MCU,Flash Memory 256 KB, SRAM 32KB, 48mhz clock, Ublok Wifi interface.
  Heart Rate Sensor: The DFRobot heart rate sensor is a thumb-sized heart rate monitor designed for Arduino microcontrollers. It includes a Gravity interface, for easy plug-and-play connectivity. This sensor is a pulse sensor which is developed based on PPG (PhotoPlethysmoGraphy) techniques. This is a simple and low-cost optical technique that can be used to detect blood volume changes in the microvascular bed of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
